# Fritzing sketch SimonSketch (saved by Fritzing 0.9.3b)
breadboards: 1

parts:
  U1 = NodeMCU V1.0
  Part1 = LCD1602-I2C
  S1 = Pushbutton [package="[SMD]"]
  S2 = Pushbutton [package="[SMD]"]
  S3 = Pushbutton [package="[SMD]"]
  S4 = Pushbutton [package="[SMD]"]
  LED1 = smd LED [color="Red (633nm)" package="0805 [SMD]"]
  LED2 = smd LED [color="Green (555nm)" package="0805 [SMD]"]
  LED3 = smd LED [color="Yellow (595nm)" package="0805 [SMD]"]
  LED4 = smd LED [color="Blue (430nm)" package="0805 [SMD]"]
  R2 = Resistor [tolerance=±5% resistance=1k package=THT]
  R3 = Resistor [tolerance=±5% resistance=1k package=THT]
  R4 = Resistor [tolerance=±5% resistance=1k package=THT]
  R5 = Resistor [tolerance=±5% resistance=1k package=THT]
  R6 = Resistor [tolerance=±5% resistance=100 package="0402 [SMD]"]
  J1 = Piezo Speaker

nets:
  N1: U1.D0, R6.Pin_1
  N2: U1.D1, Part1.SCL
  N3: U1.D2, Part1.SDA
  N4: U1.D3, S4.Pin_1, S4.Pin_2
  N5: U1.D4, S3.Pin_1, S3.Pin_2
  GND: U1.GND, Part1.GND, S1.Pin_3, S1.Pin_4, S2.Pin_3, S2.Pin_4, S3.Pin_3, S3.Pin_4, S4.Pin_3, S4.Pin_4, LED1.cathode, LED2.cathode, LED3.cathode, LED4.cathode, J1.pin1
  N6: U1.D5, R2.Pin_0
  N7: U1.D6, R3.Pin_0
  N8: U1.D7, R4.Pin_0
  N9: U1.D8, R5.Pin_0
  N10: U1.RX, S2.Pin_1, S2.Pin_2
  N11: U1.TX, S1.Pin_1, S1.Pin_2
  VIN: U1.Vin, Part1.VCC
  N12: LED1.anode, R2.Pin_1
  N13: LED2.anode, R3.Pin_1
  N14: LED3.anode, R4.Pin_1
  N15: LED4.anode, R5.Pin_1
  N16: R6.Pin_0, J1.pin2

custom parts:
  NodeMCU V1.0: ESP8266 based NodeMCU
  LCD1602-I2C: A standard character display, usually with 2x16 characters. Comes in many colors with LCM1602 IIC attached.
